# Fritzing sketch uselessbox_wiring (saved by Fritzing 0.9.3b)
breadboards: 1

parts:
  Part1 = Prototyping Shield
  S1 = Taiway 100-SP-X-T1 SPDT Miniature Toggle Switch [part_number=100-SP-X-T1-0-0-B1-M2 package=THT]
  R1 = Resistor [tolerance=±5% resistance=220 package=THT]
  R2 = Resistor [tolerance=±5% resistance=220 package=THT]
  J1 = Basic Servo

nets:
  N1: Part1.D9_PWM, J1.pulse
  N2: Part1.D10_PWM/SS, S1.L1, R2.Pin_0
  N3: Part1.D11_PWM/MOSI, S1.L2, R1.Pin_0
  N4: Part1.5V#94, J1.vcc
  N5: Part1.5V#96, S1.COM
  N6: Part1.GND#99, R2.Pin_1
  N7: Part1.GND#100, R1.Pin_1
  N8: Part1.GND#101, J1.gnd

custom parts:
  Prototyping Shield: The Arduino Uno is a microcontroller board based on the ATmega328 (datasheet). It has 14 digital input/output pins (of which 6 can be used as PWM outputs), 6 analog inputs, a 16 MHz ceramic resonator, a USB connection, a power jack, an ICSP header, and a reset button. It contains everything needed to support the microcontroller; simply connect it to a computer with a USB cable or power it with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
